// Logisim project q1_f1_NAND.circ as structural Verilog: 1 circuit, main circuit main
module main (
  input  A,
  input  B,
  input  D,
  input  C,
  output out_5
);

  wire nand_1_out, not_1_out, not_2_out;

  not not_1 (not_1_out, B);
  not not_2 (not_2_out, D);
  nand nand_1 (nand_1_out, A, not_1_out, not_2_out);
  nand nand_2 (out_5, nand_1_out, C);
endmodule
