// Logisim project q2_f_prime.circ as structural Verilog: 1 circuit, main circuit main
module main (
  input  A,
  input  B,
  input  C,
  input  D,
  output out_5
);

  wire nand_1_out, nand_2_out, nand_3_out, nand_4_out, nand_5_out, not_1_out, not_2_out, not_3_out,
       not_4_out, not_5_out;

  not not_1 (not_1_out, C);
  not not_2 (not_2_out, A);
  not not_3 (not_3_out, B);
  nand nand_1 (nand_1_out, A, D);
  nand nand_2 (nand_2_out, B, not_1_out);
  nand nand_3 (nand_3_out, not_2_out, not_3_out);
  not not_4 (not_4_out, nand_2_out);
  not not_5 (not_5_out, nand_3_out);
  nand nand_4 (nand_4_out, nand_1_out, not_4_out);
  nand nand_5 (nand_5_out, not_5_out, D);
  nand nand_6 (out_5, nand_4_out, nand_5_out);
endmodule
