// Logisim project q1_f2_NAND.circ as structural Verilog: 1 circuit, main circuit main
module main (
  input  A,
  input  B,
  input  C,
  input  D,
  output out_5
);

  wire nand_1_out, nand_2_out, nand_3_out, not_1_out, not_2_out;

  not not_1 (not_1_out, B);
  nand nand_1 (nand_1_out, A, not_1_out);
  nand nand_2 (nand_2_out, B, D);
  not not_2 (not_2_out, A);
  nand nand_3 (nand_3_out, not_2_out, C, D);
  nand nand_4 (out_5, nand_1_out, nand_2_out, nand_3_out);
endmodule
