// Logisim project q1_f1.circ as structural Verilog: 1 circuit, main circuit main
module main (
  input  A,
  input  B,
  input  C,
  input  D,
  output out_5
);

  wire and_1_out, and_2_out, not_1_out, not_2_out, not_3_out;

  not not_1 (not_1_out, B);
  not not_2 (not_2_out, C);
  not not_3 (not_3_out, D);
  and and_1 (and_1_out, A, not_1_out, not_3_out);
  buf and_2 (and_2_out, not_2_out);  // AND_Gate
  or or_1 (out_5, and_1_out, and_2_out);
endmodule
